// Digital circuit inum-to-ascii.dig as structural Verilog
module inum_to_ascii (
  input  [2:0] inum,
  output [7:0] I_3,
  output [7:0] I_2,
  output [7:0] I_1,
  output [7:0] I_0
);

  ROM #(.AddrBits(3), .Bits(32)) rom_1 (.A(inum), .sel(1'b1), .D({I_0, I_1, I_2, I_3}));
  // Probe on I_0
  // Probe on I_1
  // Probe on I_2
  // Probe on I_3

  // Notes on the sheet:
  //   contents of rom_1 (hex, n*v repeats v):
  //   41444449,41444452,4a414c5f,4a414c52,4d554c5f,5355425f,554e494d
endmodule
